// Logisim project alovt.circ as structural Verilog: 1 circuit, main circuit main
module main (
  input  [7:0] Data_In,
  input  CLK,
  input  Enable,
  output [7:0] Data_Out
);

  D_Flip_Flop d_ff_1 ();  // open: clk, D, Q, Qn, preset, en, reset
  D_Flip_Flop d_ff_2 ();  // open: clk, D, Q, Qn, preset, en, reset
  D_Flip_Flop d_ff_3 ();  // open: clk, D, Q, Qn, preset, en, reset
  D_Flip_Flop d_ff_4 ();  // open: clk, D, Q, Qn, preset, en, reset
  D_Flip_Flop d_ff_5 ();  // open: clk, D, Q, Qn, preset, en, reset
  D_Flip_Flop d_ff_6 ();  // open: clk, D, Q, Qn, preset, en, reset
  D_Flip_Flop d_ff_7 ();  // open: clk, D, Q, Qn, preset, en, reset
  D_Flip_Flop d_ff_8 ();  // open: clk, D, Q, Qn, preset, en, reset

  // Notes on the sheet:
  //   8-Bit Synchronous Register
endmodule
